# Fritzing sketch board (saved by Fritzing 0.9.10b)
stripboards: 1

parts:
  U1 = 4001 4 x 2 Input NOR Gate, single part [part_number=4001 package="DIP (Dual Inline) [THT]"]
  R1 = Resistor [tolerance=±5% power=0.25 resistance=10 package=THT]
  R2 = Resistor [tolerance=±5% power=0.25 resistance=10 package=THT]
  R3 = Resistor [tolerance=±5% power=0.25 resistance=10 package=THT]
  D1 = Rectifier Diode [part_number=1N4001 package="300 mil [THT]"]
  R4 = Resistor [tolerance=±5% power=0.25 resistance=680 package=THT]
  R5 = Resistor [tolerance=±5% power=0.25 resistance=680 package=THT]
  LED1 = RGB LED (com. cathode, rgb) [package="5 mm [THT]"]
  R6 = Resistor [tolerance=±5% power=0.25 resistance=1M package=THT]
  VCC1 = Battery
  Part1 = Arduino Uno (Rev3)
  J1 = shrouded pin header, 10 pins [form="♂ (shrouded male)"]
  J2 = female pin header, 4 pins [form="♀ (female)"]
  J3 = female pin header, 4 pins [form="♀ (female)"]
  R7 = Resistor [tolerance=±5% power=0.25 resistance=4.7k package=THT]
  R8 = Resistor [tolerance=±5% power=0.25 resistance=4.7k package=THT]
  J4 = rounded female pin header, 3 pins [form="♀ (female rounded)"]
  R9 = Resistor [tolerance=±5% power=0.25 resistance=4.7k package=THT]

nets:
  N1: U1.B1, R1.Pin_1, R2.Pin_1, R3.Pin_1, D1.anode, Part1.GND, J1.pin10, J2.pin1, J3.pin1, J4.pin3
  N2: U1.B2, D1.cathode, Part1.D10_PWM/SS, J1.pin8
  N3: U1.GND, R1.Pin_0, R2.Pin_0, R3.Pin_0
  N4: U1.B4, LED1.common_cathode, R6.Pin_1, VCC1.-
  N5: U1.VDD, R6.Pin_0, VCC1.+, Part1.A0, Part1.D13/SCK, J1.pin2, J1.pin9, J4.pin2, R9.Pin_0
  N6: R4.Pin_0, Part1.D11_PWM/MOSI, J1.pin7
  N7: R4.Pin_1, LED1.green_anode
  N8: R5.Pin_0, LED1.red_anode
  N9: R5.Pin_1, Part1.D12/MISO, J1.pin6
  N10: Part1.A1, J1.pin1
  N11: Part1.A4/SDA, J1.pin3, J2.pin2, J3.pin2, R8.Pin_0
  N12: Part1.A5/SCL, J1.pin4, J2.pin3, J3.pin3, R7.Pin_0
  N13: Part1.5V, J1.pin5, J2.pin4, J3.pin4, R7.Pin_1, R8.Pin_1, J4.pin1, R9.Pin_1
